// Logisim project lab1_adv.circ as structural Verilog: 4 circuits, main circuit dmux_2
module dmux_2 (
);

  wire [3:0] a_3_0, b_3_0, in_3_0, not_1_out, sel;

  assign not_1_out = ~sel;  // NOT_Gate not_1, 4 bits wide
  assign a_3_0 = in_3_0 & not_1_out;  // AND_Gate and_1, 4 bits wide
  assign b_3_0 = in_3_0 & sel;  // AND_Gate and_2, 4 bits wide
endmodule

module dmux_4 (
);

  wire [1:0] sel_1_0;
  wire [3:0] a_3_0, b_3_0, c_3_0, d_3_0, demultiplexer_1_out0, demultiplexer_1_out1, in_3_0;

  Demultiplexer #(.width(4), .enable("false")) demultiplexer_1 (
    .out0(demultiplexer_1_out0), .out1(demultiplexer_1_out1), .in(in_3_0), .sel(sel_1_0[1]));
  Demultiplexer #(.width(4), .enable("false")) demultiplexer_2 (
    .out0(a_3_0), .out1(b_3_0), .in(demultiplexer_1_out0), .sel(sel_1_0[0]));
  Demultiplexer #(.width(4), .enable("false")) demultiplexer_3 (
    .out0(c_3_0), .out1(d_3_0), .in(demultiplexer_1_out1), .sel(sel_1_0[0]));
endmodule

module cb_2 (
);

  wire control, not_1_out;
  wire [3:0] demultiplexer_1_out0, demultiplexer_1_out1, demultiplexer_2_out0, demultiplexer_2_out1,
       in1_4_1_0, in2_4_1_0, out1_4_1_0, out2_4_1_0;

  not not_1 (not_1_out, control);
  Demultiplexer #(.width(4), .enable("false")) demultiplexer_1 (
    .out0(demultiplexer_1_out0), .out1(demultiplexer_1_out1), .in(in1_4_1_0), .sel(control));
  Demultiplexer #(.width(4), .enable("false")) demultiplexer_2 (
    .out0(demultiplexer_2_out0), .out1(demultiplexer_2_out1), .in(in2_4_1_0), .sel(not_1_out));
  Multiplexer #(.width(4), .enable("false")) multiplexer_1 (
    .in0(demultiplexer_1_out0), .in1(demultiplexer_2_out0), .out(out1_4_1_0), .sel(control));
  Multiplexer #(.width(4), .enable("false")) multiplexer_2 (
    .in0(demultiplexer_1_out1), .in1(demultiplexer_2_out1), .out(out2_4_1_0), .sel(not_1_out));
endmodule

module cb_4 (
);

  cb_2 cb_2_1 ();
  cb_2 cb_2_2 ();
  cb_2 cb_2_3 ();
  cb_2 cb_2_4 ();
  cb_2 cb_2_5 ();
endmodule
