// Logisim project lab3_adv.circ as structural Verilog: 2 circuits, main circuit FIFO_8
module FIFO_8 (
  input  clk,
  input  rst_n,
  input  wen,
  input  ren,
  input  [7:0] din,
  output [7:0] dout,
  output error
);

  wire and_2_out, and_3_out, and_4_out, empty_out, full_out, multiplexer_6_out, nand_1_out, not_1_out,
       not_2_out, not_3_out, not_4_out, not_5_out, or_1_out;
  wire [2:0] adder_1_out, adder_2_out, adder_3_out, and_1_out, and_5_out, and_6_out, back_q, front_q,
       multiplexer_1_out, multiplexer_3_out, multiplexer_4_out, multiplexer_7_out, multiplexer_8_out,
       xnor_1_out, xnor_2_out;
  wire [7:0] multiplexer_2_out, multiplexer_5_out, ram_1_data, undriven;

  not not_1 (not_1_out, wen);
  nand nand_1 (nand_1_out, not_1_out, ren, full_out);
  not not_2 (not_2_out, empty_out);
  not not_3 (not_3_out, rst_n);
  Adder #(.width(3)) adder_1 (.a(front_q), .b(3'b001), .out(adder_1_out));  // open: cin, cout
  assign and_1_out = adder_1_out & 3'b111;  // AND_Gate and_1, 3 bits wide
  and and_2 (and_2_out, rst_n, empty_out);
  or or_1 (or_1_out, and_2_out, and_3_out);
  and and_3 (and_3_out, not_3_out, wen, full_out);
  Adder #(.width(3)) adder_2 (.a(back_q), .b(3'b001), .out(adder_2_out));  // open: cin, cout
  Multiplexer #(.width(3), .enable("false")) multiplexer_1 (
    .in0(front_q), .in1(and_1_out), .out(multiplexer_1_out), .sel(and_4_out));
  and and_4 (and_4_out, not_2_out, ren);
  Multiplexer #(.width(8), .enable("false")) multiplexer_2 (
    .in0(undriven), .out(multiplexer_2_out), .sel(nand_1_out));  // open: in1
  Multiplexer #(.width(3), .enable("false")) multiplexer_3 (
    .in0(back_q), .in1(and_5_out), .out(multiplexer_3_out), .sel(nand_1_out));
  assign and_5_out = adder_2_out & 3'b111;  // AND_Gate and_5, 3 bits wide
  Multiplexer #(.width(3), .enable("false")) multiplexer_4 (
    .in0(multiplexer_1_out), .in1(3'b000), .out(multiplexer_4_out), .sel(rst_n));
  Register #(.width(3)) front (.D(multiplexer_4_out), .Q(front_q), .clk(clk));  // open: en, clr
  Register out (.D(multiplexer_5_out), .Q(dout), .clk(clk));  // open: en, clr
  Multiplexer #(.width(8), .enable("false")) multiplexer_5 (
    .in0(multiplexer_2_out), .in1({8{1'b0}}), .out(multiplexer_5_out), .sel(rst_n));
  Multiplexer #(.enable("false")) multiplexer_6 (.in0(or_1_out), .in1(1'b0), .out(multiplexer_6_out), .sel(rst_n));
  Multiplexer #(.width(3), .enable("false")) multiplexer_7 (
    .in0(and_5_out), .in1(and_1_out), .out(multiplexer_7_out), .sel(ren));
  Multiplexer #(.width(3), .enable("false")) multiplexer_8 (
    .in0(multiplexer_3_out), .in1(3'b000), .out(multiplexer_8_out), .sel(rst_n));
  Register #(.width(3)) back (.D(multiplexer_8_out), .Q(back_q), .clk(clk));  // open: en, clr
  Register #(.width(1)) err (.D(multiplexer_6_out), .Q(error), .clk(clk));  // open: en, clr
  not not_4 (not_4_out, ren);
  Adder #(.width(3)) adder_3 (.a(back_q), .b(3'b001), .out(adder_3_out));  // open: cin, cout
  RAM #(.addrWidth(3)) ram_1 (.addr(multiplexer_7_out), .data(ram_1_data), .ld(not_4_out));  // open: sel, clk, clr
  Multiplexer #(.width(8), .enable("false")) multiplexer_9 (.in0(undriven), .in1(din), .out(ram_1_data), .sel(ren));
  assign and_6_out = adder_3_out & 3'b111;  // AND_Gate and_6, 3 bits wide
  assign xnor_1_out = ~(back_q ^ front_q);  // XNOR_Gate xnor_1, 3 bits wide
  assign xnor_2_out = ~(and_6_out ^ front_q);  // XNOR_Gate xnor_2, 3 bits wide
  and full (full_out, xnor_2_out[0], xnor_2_out[1], xnor_2_out[2]);
  not not_5 (not_5_out, full_out);
  and empty (empty_out, not_5_out, xnor_1_out[0], xnor_1_out[1], xnor_1_out[2]);
endmodule

module Round_Robin_FIFO_Arbiter (
  input  rst_n,
  input  [3:0] wen,
  input  [7:0] a,
  input  [7:0] b,
  input  [7:0] c,
  input  [7:0] d,
  output [7:0] dout,
  output valid
);

  wire and_1_out, and_2_out, and_3_out, and_4_out, and_5_out, and_7_out, and_8_out, clk_out, decoder_1_out0,
       decoder_1_out1, decoder_1_out2, decoder_1_out3, multiplexer_4_out, not_1_out, not_3_out, qa_error,
       qb_error, qc_error, qd_error, ra_q, rb_q, rc_q, rd_q;
  wire [1:0] cnt_q;
  wire [3:0] dwren_q, multiplexer_1_out, not_2_out;
  wire [7:0] multiplexer_2_out, multiplexer_3_out, qa_dout, qb_dout, qc_dout, qd_dout;

  not not_1 (not_1_out, rst_n);
  Multiplexer #(.width(4), .enable("false")) multiplexer_1 (
    .in0(wen), .in1(4'b1111), .out(multiplexer_1_out), .sel(rst_n));
  Decoder #(.select(2)) decoder_1 (
    .out0(decoder_1_out0), .out1(decoder_1_out1), .out2(decoder_1_out2), .out3(decoder_1_out3), .sel(cnt_q));  // open: en
  Counter #(.width(2), .max('h3), .ongoal("continue")) cnt (
    .load(not_1_out), .D(2'b00), .count(rst_n), .Q(cnt_q), .clk(clk_out));  // open: carry, clr
  Register #(.width(4)) dwren (.D(multiplexer_1_out), .Q(dwren_q), .clk(clk_out));  // open: en, clr
  Clock clk (.out(clk_out));
  assign not_2_out = ~wen;  // NOT_Gate not_2, 4 bits wide
  and and_1 (and_1_out, not_2_out[0], decoder_1_out0);
  Register #(.width(1)) ra (.D(and_1_out), .Q(ra_q), .clk(clk_out));  // open: en, clr
  and and_2 (and_2_out, not_2_out[1], decoder_1_out1);
  and and_3 (and_3_out, not_2_out[2], decoder_1_out2);
  and and_4 (and_4_out, not_2_out[3], decoder_1_out3);
  FIFO_8 qa (.clk(clk_out), .rst_n(rst_n), .wen(wen[0]), .ren(ra_q), .din(a), .dout(qa_dout), .error(qa_error));
  Register #(.width(1)) rb (.D(and_2_out), .Q(rb_q), .clk(clk_out));  // open: en, clr
  and and_5 (and_5_out, qa_error, dwren_q[0]);
  FIFO_8 qb (.clk(clk_out), .rst_n(rst_n), .wen(wen[1]), .ren(rb_q), .din(b), .dout(qb_dout), .error(qb_error));
  and and_6 (and_5_out, qb_error, dwren_q[1]);
  FIFO_8 qc (.clk(clk_out), .rst_n(rst_n), .wen(wen[2]), .ren(rc_q), .din(c), .dout(qc_dout), .error(qc_error));
  Register #(.width(1)) rc (.D(and_3_out), .Q(rc_q), .clk(clk_out));  // open: en, clr
  FIFO_8 qd (.clk(clk_out), .rst_n(rst_n), .wen(wen[3]), .ren(rd_q), .din(d), .dout(qd_dout), .error(qd_error));
  Register #(.width(1)) rd (.D(and_4_out), .Q(rd_q), .clk(clk_out));  // open: en, clr
  and and_7 (and_7_out, qc_error, dwren_q[2]);
  and and_8 (and_8_out, qd_error, dwren_q[3]);
  Multiplexer #(.width(8), .enable("false")) multiplexer_2 (
    .in0({8{1'b0}}), .in1(multiplexer_3_out), .out(multiplexer_2_out), .sel(not_3_out));
  Multiplexer #(.select(2), .width(8), .enable("false")) multiplexer_3 (
    .in0(qa_dout), .in1(qb_dout), .in2(qc_dout), .in3(qd_dout), .out(multiplexer_3_out), .sel(cnt_q));
  not not_3 (not_3_out, multiplexer_4_out);
  Multiplexer #(.select(2), .enable("false")) multiplexer_4 (
    .in0(and_5_out), .in1(and_5_out), .in2(and_7_out), .in3(and_8_out), .out(multiplexer_4_out), .sel(cnt_q));
  Register out (.D(multiplexer_2_out), .Q(dout), .clk(clk_out));  // open: en, clr
  Register #(.width(1)) vld (.D(not_3_out), .Q(valid), .clk(clk_out));  // open: en, clr
endmodule
